// Logisim project first.circ as structural Verilog: 1 circuit, main circuit main
module main (
  input  A,
  input  B
);

  wire and_1_out, or_1_out;

  buf and_1 (and_1_out, A);  // AND_Gate
  buf or_1 (or_1_out, B);  // OR_Gate
  LED led_1 (.in(and_1_out));
  LED led_2 (.in(or_1_out));
endmodule
